// Digital circuit Register-file-4bit.dig as structural Verilog
module Register_file_4bit (
  input  [1:0] Sel_read1,
  input  [1:0] Sel_read2,
  input  clk,
  input  [3:0] Write_data,
  input  [1:0] Sel_write,
  input  [7:0] CTRL_registers,
  output [3:0] Read_data_1,
  output [3:0] Read_data_2
);

  wire [3:0] demultiplexer_1_out_0, demultiplexer_1_out_1, demultiplexer_1_out_2, demultiplexer_1_out_3,
       R_0_p4, R_1_p4, R_2_p4, R_3_p4;

  Demultiplexer #(.Selector_Bits(2), .Bits(4)) demultiplexer_1 (
    .sel(Sel_write), .in(Write_data), .out_0(demultiplexer_1_out_0), .out_1(demultiplexer_1_out_1),
    .out_2(demultiplexer_1_out_2), .out_3(demultiplexer_1_out_3));
  // _4_bit_Register R_0: pin names not known; wires that end beside it: clk, demultiplexer_1_out_0, CTRL_registers[1:0], R_0_p4
  // _4_bit_Register R_1: pin names not known; wires that end beside it: clk, demultiplexer_1_out_1, CTRL_registers[3:2], R_1_p4
  // _4_bit_Register R_2: pin names not known; wires that end beside it: clk, demultiplexer_1_out_2, CTRL_registers[5:4], R_2_p4
  // _4_bit_Register R_3: pin names not known; wires that end beside it: clk, demultiplexer_1_out_3, CTRL_registers[7:6], R_3_p4
  Multiplexer #(.Selector_Bits(2), .Bits(4)) multiplexer_1 (
    .sel(Sel_read1), .in_0(R_0_p4), .in_1(R_1_p4), .in_2(R_2_p4), .in_3(R_3_p4), .out(Read_data_1));
  Multiplexer #(.Selector_Bits(2), .Bits(4)) multiplexer_2 (
    .sel(Sel_read2), .in_0(R_0_p4), .in_1(R_1_p4), .in_2(R_2_p4), .in_3(R_3_p4), .out(Read_data_2));
endmodule
