// Digital circuit RegisterFile_ALU.dig as structural Verilog
module RegisterFile_ALU (
  input  [2:0] S_1_S_0_C_in,
  input  clk,
  input  [1:0] Sel_read1,
  input  [1:0] Sel_read2,
  input  [3:0] Write_data,
  input  [1:0] Sel_write,
  input  [7:0] CTRL_registers,
  output overflow,
  output [3:0] D
);

  wire [3:0] register_file_4bit_1_read_data_1, register_file_4bit_1_read_data_2;

  Register_file_4bit register_file_4bit_1 (
    .Sel_read1(Sel_read1), .Sel_read2(Sel_read2), .clk(clk), .Write_data(Write_data), .Sel_write(Sel_write),
    .CTRL_registers(CTRL_registers), .Read_data_1(register_file_4bit_1_read_data_1),
    .Read_data_2(register_file_4bit_1_read_data_2));
  _4_bit_ALU _4_bit_alu_1 (
    .A(register_file_4bit_1_read_data_1), .B(register_file_4bit_1_read_data_2), .S_1_S_0_C_in(S_1_S_0_C_in),
    .D(D), .overflow(overflow));
endmodule
